// Digital circuit Gated D Latch.dig as structural Verilog
module Gated_D_Latch (
  input  D,
  input  En,
  output Q,
  output Qn
);

  wire not_1_out;

  not not_1 (not_1_out, D);
  Gated_SR_Latch gated_sr_latch_1 (.S(D), .R(not_1_out), .Clk(En), .Q(Q), .Qn(Qn));
endmodule
