// Digital circuit Gated SR Latch.dig as structural Verilog
module Gated_SR_Latch (
  input  S,
  input  R,
  input  Clk,
  output Q,
  output Qn
);

  wire nand_1_out, nand_2_out;

  nand nand_1 (nand_1_out, S, Clk);
  nand nand_2 (nand_2_out, Clk, R);
  nand nand_3 (Q, nand_1_out, Qn);
  nand nand_4 (Qn, Q, nand_2_out);
endmodule
