// Digital circuit test.dig as structural Verilog
module test (
  input  a,
  input  b,
  input  c,
  input  d,
  output f
);

  wire and_1_out, and_2_out;

  and and_1 (and_1_out, a, b);
  and and_2 (and_2_out, c, d);
  or or_1 (f, and_1_out, and_2_out);
endmodule
